// Logisim project Counter.circ as structural Verilog: 1 circuit, main circuit main
module main (
  input  in_1,
  input  in_2,
  output out_3,
  output MSB,
  output out_5,
  output MSB_2,
  output out_7,
  output out_8,
  output out_9
);

  wire clock_1_out, clock_2_out, nand_1_out, not_1_out, not_2_out, not_3_out, not_4_out, not_5_out, not_6_out;

  Clock clock_1 (.out(clock_1_out));
  Clock clock_2 (.out(clock_2_out));
  J_K_Flip_Flop j_k_ff_1 (.J(in_2), .clk(clock_1_out), .K(in_2), .Q(out_9), .reset(not_6_out));  // open: Qn, preset, en
  J_K_Flip_Flop j_k_ff_2 (.J(in_1), .clk(clock_2_out), .K(in_1), .Q(out_3));  // open: Qn, preset, en, reset
  not not_1 (not_1_out, out_9);
  not not_2 (not_2_out, out_3);
  J_K_Flip_Flop j_k_ff_3 (.J(in_2), .clk(not_1_out), .K(in_2), .Q(out_8), .reset(not_6_out));  // open: Qn, preset, en
  J_K_Flip_Flop j_k_ff_4 (.J(in_1), .clk(not_2_out), .K(in_1), .Q(out_5));  // open: Qn, preset, en, reset
  not not_3 (not_3_out, out_8);
  not not_4 (not_4_out, out_5);
  J_K_Flip_Flop j_k_ff_5 (.J(in_2), .clk(not_3_out), .K(in_2), .Q(out_7), .reset(not_6_out));  // open: Qn, preset, en
  J_K_Flip_Flop j_k_ff_6 (.J(in_1), .clk(not_4_out), .K(in_1), .Q(MSB));  // open: Qn, preset, en, reset
  not not_5 (not_5_out, out_7);
  J_K_Flip_Flop j_k_ff_7 (.J(in_2), .clk(not_5_out), .K(in_2), .Q(MSB_2), .reset(not_6_out));  // open: Qn, preset, en
  nand nand_1 (nand_1_out, out_8, MSB_2);
  not not_6 (not_6_out, nand_1_out);
endmodule
