// Logisim project Q1.circ as structural Verilog: 1 circuit, main circuit main
module main (
  input  X,
  input  Y,
  output A,
  output B,
  output Z
);

  wire and_1_out, and_2_out, and_3_out, and_4_out, clock_1_out, not_1_out, not_2_out, or_1_out, or_2_out;

  not not_1 (not_1_out, X);
  and and_1 (and_1_out, A, X);
  and and_2 (and_2_out, not_1_out, Y);
  and and_3 (and_3_out, B, not_2_out);
  not not_2 (not_2_out, X);
  and and_4 (and_4_out, A, X);
  or or_1 (or_1_out, and_1_out, and_2_out);
  or or_2 (or_2_out, and_3_out, and_4_out);
  Clock clock_1 (.out(clock_1_out));
  D_Flip_Flop d_ff_1 (.clk(or_1_out), .D(clock_1_out), .Q(A));  // open: Qn, preset, en, reset
  D_Flip_Flop d_ff_2 (.clk(or_2_out), .D(clock_1_out), .Q(B));  // open: Qn, preset, en, reset

  assign Z = B;
endmodule
