// Logisim project Q2.circ as structural Verilog: 1 circuit, main circuit main
module main (
  input  I3,
  input  I2,
  input  I1,
  input  I0,
  input  Load,
  input  Clock,
  output Q3,
  output Q2,
  output Q1,
  output Q0
);

  wire multiplexer_1_out, multiplexer_2_out, multiplexer_3_out, multiplexer_4_out;

  Multiplexer multiplexer_1 (.in0(Q3), .in1(I3), .out(multiplexer_1_out), .sel(Load));  // open: en
  Multiplexer multiplexer_2 (.in0(Q2), .in1(I2), .out(multiplexer_2_out), .sel(Load));  // open: en
  D_Flip_Flop d_ff_1 (.clk(Clock), .D(multiplexer_1_out), .Q(Q3));  // open: Qn, preset, en, reset
  Multiplexer multiplexer_3 (.in0(Q1), .in1(I1), .out(multiplexer_3_out), .sel(Load));  // open: en
  D_Flip_Flop d_ff_2 (.clk(Clock), .D(multiplexer_2_out), .Q(Q2));  // open: Qn, preset, en, reset
  Multiplexer multiplexer_4 (.in0(Q0), .in1(I0), .out(multiplexer_4_out), .sel(Load));  // open: en
  D_Flip_Flop d_ff_3 (.clk(Clock), .D(multiplexer_3_out), .Q(Q1));  // open: Qn, preset, en, reset
  D_Flip_Flop d_ff_4 (.clk(Clock), .D(multiplexer_4_out), .Q(Q0));  // open: Qn, preset, en, reset
endmodule
