// Logisim project lab 08 Buss REg.circ as structural Verilog: 1 circuit, main circuit main
module main (
  input  [1:0] S1_S0,
  input  [3:0] DD,
  input  [3:0] DC,
  input  [3:0] DB,
  input  [3:0] DA,
  input  en,
  input  en_2,
  input  en_3,
  input  en_4,
  input  Load,
  input  Load_2,
  input  Load_3,
  input  Load_4,
  output [3:0] out_14,
  output [3:0] out_15,
  output [3:0] out_16
);

  wire clock_1_out;
  wire [3:0] register_2_q, register_3_q, register_5_q, register_7_q;

  Clock clock_1 (.out(clock_1_out));
  Register #(.width(4)) register_1 (.D(out_14), .en(Load), .Q(out_15), .clk(clock_1_out));  // open: clr
  Multiplexer #(.select(2)) multiplexer_1 (
    .in0(register_7_q[3]), .in1(register_5_q[3]), .in2(register_3_q[3]), .in3(register_2_q[3]),
    .out(out_14[3]), .sel(S1_S0));  // open: en
  Register #(.width(4)) register_2 (.D(DD), .en(en), .Q(register_2_q), .clk(clock_1_out));  // open: clr
  Multiplexer #(.select(2)) multiplexer_2 (
    .in0(register_7_q[2]), .in1(register_5_q[2]), .in2(register_3_q[2]), .in3(register_2_q[2]),
    .out(out_14[2]), .sel(S1_S0));  // open: en
  Multiplexer #(.select(2)) multiplexer_3 (
    .in0(register_7_q[1]), .in1(register_5_q[1]), .in2(register_3_q[1]), .in3(register_2_q[1]),
    .out(out_14[1]), .sel(S1_S0));  // open: en
  Register #(.width(4)) register_3 (.D(DC), .en(en_2), .Q(register_3_q), .clk(clock_1_out));  // open: clr
  Register #(.width(4)) register_4 (.D(out_14), .en(Load_2), .clk(clock_1_out));  // open: Q, clr
  Multiplexer #(.select(2)) multiplexer_4 (
    .in0(register_7_q[0]), .in1(register_5_q[0]), .in2(register_3_q[0]), .in3(register_2_q[0]),
    .out(out_14[0]), .sel(S1_S0));  // open: en
  Register #(.width(4)) register_5 (.D(DB), .en(en_3), .Q(register_5_q), .clk(clock_1_out));  // open: clr
  Register #(.width(4)) register_6 (.D(out_14), .en(Load_3), .Q(out_16), .clk(clock_1_out));  // open: clr
  Register #(.width(4)) register_7 (.D(DA), .en(en_4), .Q(register_7_q), .clk(clock_1_out));  // open: clr
  Register #(.width(4)) register_8 (.D(out_14), .en(Load_4), .clk(clock_1_out));  // open: Q, clr
endmodule
