// Logisim project my final project inshallah.circ as structural Verilog: 1 circuit, main circuit main
module main (
  input  [3:0] FS,
  input  [7:0] X,
  input  [7:0] Y,
  output [7:0] out_4,
  output N,
  output Z,
  output V,
  output C
);

  wire adder_1_cout, adder_2_cout, adder_3_cout, adder_4_cout, adder_5_cout, adder_6_cout, adder_7_cout;
  wire [6:0] adder_1_out;
  wire [7:0] multiplexer_1_out, multiplexer_2_out, not_1_out, or_1_out, X___Y_out, X_prime_out, xor_1_out;

  assign not_1_out = ~Y;  // NOT_Gate not_1, 8 bits wide
  Multiplexer #(.select(2), .width(8)) multiplexer_1 (
    .in0({8{1'b0}}), .in1(not_1_out), .in2(Y), .in3({8{1'b1}}), .out(multiplexer_1_out), .sel(FS[2:1]));  // open: en
  assign X___Y_out = X & Y;  // AND_Gate X___Y, 8 bits wide
  assign or_1_out = X | Y;  // OR_Gate or_1, 8 bits wide
  assign xor_1_out = X ^ Y;  // XOR_Gate xor_1, 8 bits wide
  assign X_prime_out = ~X;  // NOT_Gate X_prime, 8 bits wide
  Adder #(.width(1)) adder_1 (
    .a(X[0]), .b(multiplexer_1_out[0]), .out(adder_1_out[0]), .cin(FS[0]), .cout(adder_1_cout));
  Adder #(.width(1)) adder_2 (
    .a(X[1]), .b(multiplexer_1_out[1]), .out(adder_1_out[1]), .cin(adder_1_cout), .cout(adder_2_cout));
  Adder #(.width(1)) adder_3 (
    .a(X[2]), .b(multiplexer_1_out[2]), .out(adder_1_out[2]), .cin(adder_2_cout), .cout(adder_3_cout));
  Adder #(.width(1)) adder_4 (
    .a(X[3]), .b(multiplexer_1_out[3]), .out(adder_1_out[3]), .cin(adder_3_cout), .cout(adder_4_cout));
  Adder #(.width(1)) adder_5 (
    .a(X[4]), .b(multiplexer_1_out[4]), .out(adder_1_out[4]), .cin(adder_4_cout), .cout(adder_5_cout));
  Adder #(.width(1)) adder_6 (
    .a(X[5]), .b(multiplexer_1_out[5]), .out(adder_1_out[5]), .cin(adder_5_cout), .cout(adder_6_cout));
  Adder #(.width(1)) adder_7 (
    .a(X[6]), .b(multiplexer_1_out[6]), .out(adder_1_out[6]), .cin(adder_6_cout), .cout(adder_7_cout));
  Adder #(.width(1)) adder_8 (.a(X[7]), .b(multiplexer_1_out[7]), .out(N), .cin(adder_7_cout), .cout(C));
  Multiplexer #(.select(3), .width(8)) multiplexer_2 (
    .in0(X___Y_out), .in1(or_1_out), .in2(xor_1_out), .in3(X_prime_out), .in4(Y), .in5({Y[0], Y[7:1]}),
    .in6({Y[6:0], Y[7]}), .in7(Y), .out(multiplexer_2_out), .sel(FS[2:0]));  // open: en
  Multiplexer #(.width(8)) multiplexer_3 (
    .in0({N, adder_1_out}), .in1(multiplexer_2_out), .out(out_4), .sel(FS[3]));  // open: en
  xor xor_2 (V, adder_7_cout, C);
  nor nor_1 (Z, out_4[0], out_4[1], out_4[2], out_4[3], out_4[4], out_4[5], out_4[6], out_4[7]);

  // Notes on the sheet:
  //   was 03
  //   sr B (rotate right)
  //   sl B (rotate left)
  //   1000 A and B
  //   1001 A or B
  //   1010 A xor B
  //   1011 A"
  //   1100 B
  //   1101 sr B (rotate right)
  //   1110 sl B (rotate left)
  //   0000  A
  //   0001 A + 1
  //   0010 A + B"
  //   0011 A + B" + 1
  //   0100 A + B
  //   0101 A + B + 1
  //   0110 A - 1
  //   0111 A
endmodule
